// Logisim project ALU (1).circ as structural Verilog
// ALU
module _1_bit_ALU (
  input  B,
  input  A,
  input  C_In,
  input  [1:0] AluOP,
  output Ouput,
  output C_out
);

  wire adder_1_cout, adder_1_out, and_1_out, and_2_out, or_1_out, subtractor_1_bout, subtractor_1_out;

  Subtractor #(.width(1)) subtractor_1 (.a(A), .b(B), .out(subtractor_1_out), .bin(C_In), .bout(subtractor_1_bout));
  Multiplexer multiplexer_1 (.in0(adder_1_cout), .in1(subtractor_1_bout), .out(C_out), .sel(and_1_out));  // open: en
  and and_1 (and_1_out, AluOP[1], AluOP[0]);
  and and_2 (and_2_out, A, B);
  or or_1 (or_1_out, A, B);
  Adder #(.width(1)) adder_1 (.a(A), .b(B), .out(adder_1_out), .cin(C_In), .cout(adder_1_cout));
  Multiplexer #(.select(2)) multiplexer_2 (
    .in0(and_2_out), .in1(or_1_out), .in2(adder_1_out), .in3(subtractor_1_out), .out(Ouput), .sel(AluOP));  // open: en
endmodule

// ALU
module _4_bit_ALU (
  input  C_in,
  input  [3:0] A,
  input  [3:0] B,
  input  [1:0] AluOP,
  output [3:0] \output ,
  output C_out
);

  wire n1_bit_alu_1_c_out, n1_bit_alu_2_c_out, n1_bit_alu_3_c_out;

  _1_bit_ALU u_1_bit_alu_1 (
    .Ouput(\output [0]), .B(B[0]), .A(A[0]), .C_In(C_in), .C_out(n1_bit_alu_1_c_out), .AluOP(AluOP));
  _1_bit_ALU u_1_bit_alu_2 (
    .Ouput(\output [1]), .B(B[1]), .A(A[1]), .C_In(n1_bit_alu_1_c_out), .C_out(n1_bit_alu_2_c_out),
    .AluOP(AluOP));
  _1_bit_ALU u_1_bit_alu_3 (
    .Ouput(\output [2]), .B(B[2]), .A(A[2]), .C_In(n1_bit_alu_2_c_out), .C_out(n1_bit_alu_3_c_out),
    .AluOP(AluOP));
  _1_bit_ALU u_1_bit_alu_4 (
    .Ouput(\output [3]), .B(B[3]), .A(A[3]), .C_In(n1_bit_alu_3_c_out), .C_out(C_out), .AluOP(AluOP));

  // Other names for the same wires on the sheet: OP[1:0] = AluOP
endmodule

module _32_bit_ALU (
  input  [31:0] A,
  input  [31:0] B,
  input  [1:0] AluOP,
  output [31:0] \output ,
  output Zero,
  output Overflow
);

  wire n4_bit_alu_1_c_out, n4_bit_alu_2_c_out, n4_bit_alu_3_c_out, n4_bit_alu_4_c_out, n4_bit_alu_5_c_out,
       n4_bit_alu_6_c_out, n4_bit_alu_7_c_out;

  _4_bit_ALU u_4_bit_alu_1 (
    .AluOP(AluOP), .\output (\output [3:0]), .C_out(n4_bit_alu_1_c_out), .A(A[3:0]), .B(B[3:0]), .C_in(1'b0));
  _4_bit_ALU u_4_bit_alu_2 (
    .AluOP(AluOP), .\output (\output [7:4]), .C_out(n4_bit_alu_2_c_out), .A(A[7:4]), .B(B[7:4]),
    .C_in(n4_bit_alu_1_c_out));
  _4_bit_ALU u_4_bit_alu_3 (
    .AluOP(AluOP), .\output (\output [11:8]), .C_out(n4_bit_alu_3_c_out), .A(A[11:8]), .B(B[11:8]),
    .C_in(n4_bit_alu_2_c_out));
  _4_bit_ALU u_4_bit_alu_4 (
    .AluOP(AluOP), .\output (\output [15:12]), .C_out(n4_bit_alu_4_c_out), .A(A[15:12]), .B(B[15:12]),
    .C_in(n4_bit_alu_3_c_out));
  _4_bit_ALU u_4_bit_alu_5 (
    .AluOP(AluOP), .\output (\output [19:16]), .C_out(n4_bit_alu_5_c_out), .A(A[19:16]), .B(B[19:16]),
    .C_in(n4_bit_alu_4_c_out));
  _4_bit_ALU u_4_bit_alu_6 (
    .AluOP(AluOP), .\output (\output [23:20]), .C_out(n4_bit_alu_6_c_out), .A(A[23:20]), .B(B[23:20]),
    .C_in(n4_bit_alu_5_c_out));
  _4_bit_ALU u_4_bit_alu_7 (
    .AluOP(AluOP), .\output (\output [27:24]), .C_out(n4_bit_alu_7_c_out), .A(A[27:24]), .B(B[27:24]),
    .C_in(n4_bit_alu_6_c_out));
  _4_bit_ALU u_4_bit_alu_8 (
    .AluOP(AluOP), .\output (\output [31:28]), .C_out(Overflow), .A(A[31:28]), .B(B[31:28]),
    .C_in(n4_bit_alu_7_c_out));
  nor nor_1 (Zero, \output [0], \output [1], \output [2], \output [3], \output [4], \output [5], \output [6], \output [7], \output [8], \output [9], \output [10], \output [11], \output [12], \output [13], \output [14], \output [15], \output [16], \output [17], \output [18], \output [19], \output [20], \output [21], \output [22], \output [23], \output [24], \output [25], \output [26], \output [27], \output [28], \output [29], \output [30], \output [31]);

  // Other names for the same wires on the sheet: A0_3[3:0] = A[3:0]; A4_7[3:0] = A[7:4]; A8_11[3:0] = A[11:8];
  //   A12_15[3:0] = A[15:12]; A16_19[3:0] = A[19:16]; A20_23[3:0] = A[23:20]; A24_27[3:0] = A[27:24];
  //   A28_31[3:0] = A[31:28]; B0_3[3:0] = B[3:0]; B4_7[3:0] = B[7:4]; B8_11[3:0] = B[11:8]; B12_15[3:0] = B[15:12];
  //   B16_19[3:0] = B[19:16]; B20_23[3:0] = B[23:20]; B24_27[3:0] = B[27:24]; B28_31[3:0] = B[31:28]; OP[1:0] = AluOP
endmodule
