// Logisim project Computer.circ as structural Verilog: 1 circuit, main circuit main
// in_PC
module main (
  input  [7:0] in_PC,
  output [7:0] out_PC_Plus_4,
  output [7:0] out_PC,
  output [7:0] out_MUX,
  output [7:0] out_branch_target,
  output [31:0] out_6
);

  wire ALUSrc, and_1_out, Branch, clk_t, clock_1_out, Jump, MemRead, MemtoReg, MemWrite, RegDst, RegWrite,
       ZeroFlag;
  wire [1:0] ALUCont, ALUOP;
  wire [4:0] multiplexer_2_out;
  wire [7:0] in_branch_offset_t, multiplexer_1_out, shifter_1_out;
  wire [31:0] bit_extender_1_out, main_1_out_2, main_2_out_5, multiplexer_4_out, Multiply_Out,
       register_1_read_data_1, register_1_read_data_2, WriteData;

  ROM_main main_1 (.in_1(out_PC), .out_2(main_1_out_2));
  Multiplexer #(.width(8), .enable("false")) multiplexer_1 (
    .in0(out_PC_Plus_4), .in1(out_branch_target), .out(multiplexer_1_out), .sel(and_1_out));
  and and_1 (and_1_out, Branch, ZeroFlag);
  Shifter shifter_1 (.in(main_1_out_2[7:0]), .\dist (3'b010), .out(shifter_1_out));
  Multiplexer #(.width(5), .enable("false")) multiplexer_2 (
    .in0(main_1_out_2[20:16]), .in1(main_1_out_2[15:11]), .out(multiplexer_2_out), .sel(RegDst));
  Multiplexer #(.width(8), .enable("false")) multiplexer_3 (
    .in0(multiplexer_1_out), .in1(shifter_1_out), .out(out_MUX), .sel(Jump));
  ControlUnit controlunit_1 (
    .Instruction(main_1_out_2), .RegDst(RegDst), .Branch(Branch), .Jump(Jump), .MemRead(MemRead),
    .MemtoReg(MemtoReg), .AluOP(ALUOP), .MemWrite(MemWrite), .AluSrc(ALUSrc), .RegWrite(RegWrite));
  register register_1 (
    .read_register_1(main_1_out_2[25:21]), .read_register_2(main_1_out_2[20:16]),
    .write_register(multiplexer_2_out), .write_data(WriteData), .read_data_1(register_1_read_data_1),
    .read_data_2(register_1_read_data_2), .reg_write(RegWrite), .clock(clock_1_out));
  Clock clock_1 (.out(clock_1_out));
  assign bit_extender_1_out = {{16{1'b0}}, main_1_out_2[15:0]};  // Bit_Extender bit_extender_1
  Multiplexer #(.width(32), .enable("false")) multiplexer_4 (
    .in0(register_1_read_data_2), .in1(bit_extender_1_out), .out(multiplexer_4_out), .sel(ALUSrc));
  AluControl alucontrol_1 (.AluOP(ALUOP), .Instruction(main_1_out_2[5:0]), .AluControl(ALUCont));  // open: out_4
  Shifter #(.width(32)) shifter_2 (.in(bit_extender_1_out), .\dist (5'b00010), .out(Multiply_Out));
  _32_bit_ALU u_32_bit_alu_1 (
    .A(register_1_read_data_1), .B(multiplexer_4_out), .AluOP(ALUCont), .\output (out_6), .Zero(ZeroFlag));  // open: Overflow
  Clock clock_2 (.out(clk_t));
  Register register_2 (.D(out_MUX), .en(1'b1), .Q(out_PC), .clk(clk_t));  // open: clr
  Bit_Extender #(.in_width(32), .out_width(8)) bit_extender_2 (.in(Multiply_Out), .out(in_branch_offset_t));
  RAM_main main_2 (
    .in_1(out_6[11:2]), .in_2(register_1_read_data_2), .out_5(main_2_out_5), .in_4(MemRead), .in_3(MemWrite));
  Adder adder_1 (.a(out_PC), .b(8'h4), .out(out_PC_Plus_4));  // open: cin, cout
  Multiplexer #(.width(32), .enable("false")) multiplexer_5 (
    .in0(out_6), .in1(main_2_out_5), .out(WriteData), .sel(MemtoReg));
  Adder adder_2 (.a(out_PC), .b(in_branch_offset_t), .out(out_branch_target));  // open: cin, cout

  // Other names for the same wires on the sheet: in_PC_t[7:0] = in_PC; out_branch_target_t[7:0] = out_branch_target;
  //   out_MUX_t[7:0] = out_MUX; out_PC_Plus_4_t[7:0] = out_PC_Plus_4; out_PC_t[7:0] = out_PC
endmodule
