// Logisim project ControlUnit.circ as structural Verilog
module ControlUnit (
  input  [31:0] Instruction,
  output RegDst,
  output Branch,
  output Jump,
  output MemRead,
  output MemtoReg,
  output [1:0] AluOP,
  output MemWrite,
  output AluSrc,
  output RegWrite
);

  wire isInstruction, not_1_out, not_2_out, not_3_out, not_4_out, not_5_out, not_6_out, not_7_out, or_3_out;

  or or_1 (isInstruction, Instruction[0], Instruction[1], Instruction[2], Instruction[3], Instruction[4], Instruction[5], Instruction[6], Instruction[7], Instruction[8], Instruction[9], Instruction[10], Instruction[11], Instruction[12], Instruction[13], Instruction[14], Instruction[15], Instruction[16], Instruction[17], Instruction[18], Instruction[19], Instruction[20], Instruction[21], Instruction[22], Instruction[23], Instruction[24], Instruction[25]);
  not not_1 (not_1_out, Instruction[30]);
  not not_2 (not_2_out, Instruction[30]);
  not not_3 (not_3_out, Instruction[28]);
  and LW (MemRead, Instruction[26], Instruction[27], not_3_out, not_4_out, not_1_out, Instruction[31]);
  not not_4 (not_4_out, Instruction[29]);
  not not_5 (not_5_out, Instruction[28]);
  and SW (MemWrite, Instruction[26], Instruction[27], not_5_out, Instruction[29], not_2_out, Instruction[31]);
  not not_6 (not_6_out, Instruction[28]);
  not not_7 (not_7_out, Instruction[27]);
  nor u_Jump (Jump, Instruction[26], not_7_out, Instruction[28], Instruction[29], Instruction[30], Instruction[31]);
  nor R_Type (AluOP[1], Instruction[26], Instruction[27], Instruction[28], Instruction[29], Instruction[30], Instruction[31]);
  nor BEQ (AluOP[0], Instruction[26], Instruction[27], not_6_out, Instruction[29], Instruction[30], Instruction[31]);
  and and_1 (RegDst, isInstruction, AluOP[1]);
  or or_2 (AluSrc, MemWrite, MemRead);
  or or_3 (or_3_out, MemRead, AluOP[1]);
  and and_2 (RegWrite, or_3_out, isInstruction);

  assign Branch = AluOP[0];
  assign MemtoReg = MemRead;

  // Other names for the same wires on the sheet: I0 = Instruction[26]; I1 = Instruction[27]; I2 = Instruction[28];
  //   I3 = Instruction[29]; I4 = Instruction[30]; I5 = Instruction[31]
endmodule

module AluControl (
  input  [1:0] AluOP,
  input  [5:0] Instruction,
  output [1:0] AluControl,
  output [1:0] out_4
);

  wire Add_out, not_1_out, not_2_out, not_3_out, not_4_out, not_5_out, not_6_out, not_7_out, not_8_out,
       OR_out, Sub_out;

  not not_1 (not_1_out, Instruction[5]);
  not not_2 (not_2_out, Instruction[1]);
  not not_3 (not_3_out, Instruction[5]);
  not not_4 (not_4_out, Instruction[2]);
  not not_5 (not_5_out, Instruction[5]);
  not not_6 (not_6_out, Instruction[0]);
  not not_7 (not_7_out, Instruction[2]);
  not not_8 (not_8_out, Instruction[5]);
  nor Add (Add_out, Instruction[0], Instruction[1], Instruction[2], Instruction[3], Instruction[4], not_1_out);
  nor Sub (Sub_out, Instruction[0], not_2_out, Instruction[2], Instruction[3], Instruction[4], not_3_out);
  // NOR_Gate And has open pins: in0=Instruction[0], in1=Instruction[1], in2=not_4_out, in3=Instruction[3], in4=Instruction[4], in5=not_5_out, out=open
  nor OR (OR_out, not_6_out, Instruction[1], not_7_out, Instruction[3], Instruction[4], not_8_out);
  Multiplexer #(.select(2), .width(2)) multiplexer_1 (
    .in0(2'b10), .in1(2'b11), .in2(out_4), .out(AluControl), .sel(AluOP));  // open: in3, en
  or or_2 (out_4[1], Add_out, Sub_out);
  or or_3 (out_4[0], Sub_out, OR_out);

  // Other names for the same wires on the sheet: Func[1:0] = out_4; I0 = Instruction[0]; I1 = Instruction[1];
  //   I2 = Instruction[2]; I3 = Instruction[3]; I4 = Instruction[4]; I5 = Instruction[5]
endmodule
