// Logisim project PC.circ as structural Verilog: 1 circuit, main circuit main
// in_PC
module main (
  input  [31:0] in_branch_offset,
  input  [31:0] in_PC,
  input  clk,
  input  PC_Src,
  output [31:0] out_PC_Plus_4,
  output [31:0] out_PC,
  output [31:0] out_branch_target,
  output [31:0] out_MUX
);

  Register #(.width(32)) register_1 (.D(out_MUX), .en(1'b1), .Q(out_PC), .clk(clk));  // open: clr
  // ControlUnit controlunit_1: pin names not known
  // register register_2: pin names not known
  Adder #(.width(32)) adder_1 (.a(out_PC), .b(32'h4), .out(out_PC_Plus_4));  // open: cin, cout
  Multiplexer #(.width(32), .enable("false")) multiplexer_1 (
    .in0(out_PC_Plus_4), .in1(out_branch_target), .out(out_MUX), .sel(PC_Src));
  // _32_bit_ALU 32_bit_alu_1: pin names not known
  // AluControl alucontrol_1: pin names not known
  Adder #(.width(32)) adder_2 (.a(out_PC), .b(in_branch_offset), .out(out_branch_target));  // open: cin, cout

  // Other names for the same wires on the sheet: clk_t = clk; in_branch_offset_t[31:0] = in_branch_offset;
  //   in_PC_t[31:0] = in_PC; out_branch_target_t[31:0] = out_branch_target; out_MUX_t[31:0] = out_MUX;
  //   out_PC_Plus_4_t[31:0] = out_PC_Plus_4; out_PC_t[31:0] = out_PC
endmodule
