// Logisim project RAM.circ as structural Verilog: 1 circuit, main circuit main
module main (
  input  [9:0] in_1,
  input  [31:0] in_2,
  input  in_3,
  input  in_4,
  output [31:0] out_5
);

  wire clock_1_out;

  Clock clock_1 (.out(clock_1_out));
  RAM #(.addrWidth(10), .dataWidth(32), .bus("separate")) ram_1 (
    .addr(in_1), .din(in_2), .data(out_5), .str(in_3), .sel(1'b1), .clk(clock_1_out), .ld(in_4));  // open: clr
endmodule
