// Logisim project ROM.circ as structural Verilog: 1 circuit, main circuit main
module main (
  input  [7:0] in_1,
  output [31:0] out_2
);

  ROM #(.dataWidth(32)) rom_1 (.addr(in_1), .data(out_2), .sel(1'b1));
endmodule
