// Logisim project Register File (1).circ as structural Verilog: 1 circuit, main circuit register
module register (
  input  [4:0] read_register_1,
  input  [4:0] read_register_2,
  input  [4:0] write_register,
  input  reg_write,
  input  clock,
  input  [31:0] write_data,
  output [31:0] read_data_1,
  output [31:0] read_data_2
);

  wire _1, _2, _3, _4, _5, _6, _7, _8, _9, _10, _11, _12, _13, _14, _15, _16, _17, _18, _19, _20, _21, _22,
       _23, _24, _25, _26, _27, _28, _29, _30, _31, _32, and_1_out, and_2_out, and_3_out, and_4_out,
       and_5_out, and_6_out, and_7_out, and_8_out, and_9_out, and_10_out, and_11_out, and_12_out, and_13_out,
       and_14_out, and_15_out, and_16_out, and_17_out, and_18_out, and_19_out, and_20_out, and_21_out,
       and_22_out, and_23_out, and_24_out, and_25_out, and_26_out, and_27_out, and_28_out, and_29_out,
       and_30_out, and_31_out, and_32_out;
  wire [31:0] _1O, _2O, _3O, _4O, _5O, _6O, _7O, _8O, _9O, _10O, _11O, _12O, _13O, _14O, _15O, _16O, _17O,
       _18O, _19O, _20O, _21O, _22O, _23O, _24O, _25O, _26O, _27O, _28O, _29O, _30O, _31O, _32O;

  Decoder #(.select(5)) decoder_1 (
    .out0(_1), .out1(_2), .out2(_3), .out3(_4), .out4(_5), .out5(_6), .out6(_7), .out7(_8), .out8(_9),
    .out9(_10), .out10(_11), .out11(_12), .out12(_13), .out13(_14), .out14(_15), .out15(_16), .out16(_17),
    .out17(_18), .out18(_19), .out19(_20), .out20(_21), .out21(_22), .out22(_23), .out23(_24), .out24(_25),
    .out25(_26), .out26(_27), .out27(_28), .out28(_29), .out29(_30), .out30(_31), .out31(_32),
    .sel(write_register));  // open: en
  and and_1 (and_1_out, _1, reg_write);
  and and_2 (and_2_out, _2, reg_write);
  and and_3 (and_3_out, _3, reg_write);
  and and_4 (and_4_out, _4, reg_write);
  Register #(.width(32)) register_1 (.D(write_data), .Q(_1O), .clk(clock), .clr(and_1_out));  // open: en
  Register #(.width(32)) register_2 (.D(write_data), .Q(_2O), .clk(clock), .clr(and_2_out));  // open: en
  Register #(.width(32)) register_3 (.D(write_data), .Q(_3O), .clk(clock), .clr(and_3_out));  // open: en
  Register #(.width(32)) register_4 (.D(write_data), .Q(_4O), .clk(clock), .clr(and_4_out));  // open: en
  and and_5 (and_5_out, _5, reg_write);
  and and_6 (and_6_out, _6, reg_write);
  and and_7 (and_7_out, _7, reg_write);
  and and_8 (and_8_out, _8, reg_write);
  Register #(.width(32)) register_5 (.D(write_data), .Q(_5O), .clk(clock), .clr(and_5_out));  // open: en
  Register #(.width(32)) register_6 (.D(write_data), .Q(_6O), .clk(clock), .clr(and_6_out));  // open: en
  Register #(.width(32)) register_7 (.D(write_data), .Q(_7O), .clk(clock), .clr(and_7_out));  // open: en
  Register #(.width(32)) register_8 (.D(write_data), .Q(_8O), .clk(clock), .clr(and_8_out));  // open: en
  and and_9 (and_9_out, _9, reg_write);
  Register #(.width(32)) register_9 (.D(write_data), .Q(_9O), .clk(clock), .clr(and_9_out));  // open: en
  Register #(.width(32)) register_10 (.D(write_data), .Q(_10O), .clk(clock), .clr(and_10_out));  // open: en
  and and_10 (and_10_out, _10, reg_write);
  Register #(.width(32)) register_11 (.D(write_data), .Q(_11O), .clk(clock), .clr(and_11_out));  // open: en
  and and_11 (and_11_out, _11, reg_write);
  Register #(.width(32)) register_12 (.D(write_data), .Q(_12O), .clk(clock), .clr(and_12_out));  // open: en
  and and_12 (and_12_out, _12, reg_write);
  and and_13 (and_13_out, _13, reg_write);
  and and_14 (and_14_out, _14, reg_write);
  and and_15 (and_15_out, _15, reg_write);
  and and_16 (and_16_out, _16, reg_write);
  Register #(.width(32)) register_13 (.D(write_data), .Q(_13O), .clk(clock), .clr(and_13_out));  // open: en
  Register #(.width(32)) register_14 (.D(write_data), .Q(_14O), .clk(clock), .clr(and_14_out));  // open: en
  Register #(.width(32)) register_15 (.D(write_data), .Q(_15O), .clk(clock), .clr(and_15_out));  // open: en
  Register #(.width(32)) register_16 (.D(write_data), .Q(_16O), .clk(clock), .clr(and_16_out));  // open: en
  and and_17 (and_17_out, _17, reg_write);
  and and_18 (and_18_out, _18, reg_write);
  and and_19 (and_19_out, _19, reg_write);
  and and_20 (and_20_out, _20, reg_write);
  Register #(.width(32)) register_17 (.D(write_data), .Q(_17O), .clk(clock), .clr(and_17_out));  // open: en
  Register #(.width(32)) register_18 (.D(write_data), .Q(_18O), .clk(clock), .clr(and_18_out));  // open: en
  Register #(.width(32)) register_19 (.D(write_data), .Q(_19O), .clk(clock), .clr(and_19_out));  // open: en
  Register #(.width(32)) register_20 (.D(write_data), .Q(_20O), .clk(clock), .clr(and_20_out));  // open: en
  and and_21 (and_21_out, _21, reg_write);
  and and_22 (and_22_out, _22, reg_write);
  and and_23 (and_23_out, _23, reg_write);
  and and_24 (and_24_out, _24, reg_write);
  Register #(.width(32)) register_21 (.D(write_data), .Q(_21O), .clk(clock), .clr(and_21_out));  // open: en
  Register #(.width(32)) register_22 (.D(write_data), .Q(_22O), .clk(clock), .clr(and_22_out));  // open: en
  Register #(.width(32)) register_23 (.D(write_data), .Q(_23O), .clk(clock), .clr(and_23_out));  // open: en
  Register #(.width(32)) register_24 (.D(write_data), .Q(_24O), .clk(clock), .clr(and_24_out));  // open: en
  Register #(.width(32)) register_25 (.D(write_data), .Q(_25O), .clk(clock), .clr(and_25_out));  // open: en
  and and_25 (and_25_out, _25, reg_write);
  and and_26 (and_26_out, _26, reg_write);
  Register #(.width(32)) register_26 (.D(write_data), .Q(_26O), .clk(clock), .clr(and_26_out));  // open: en
  Register #(.width(32)) register_27 (.D(write_data), .Q(_27O), .clk(clock), .clr(and_27_out));  // open: en
  and and_27 (and_27_out, _27, reg_write);
  and and_28 (and_28_out, _28, reg_write);
  Register #(.width(32)) register_28 (.D(write_data), .Q(_28O), .clk(clock), .clr(and_28_out));  // open: en
  and and_29 (and_29_out, _29, reg_write);
  and and_30 (and_30_out, _30, reg_write);
  and and_31 (and_31_out, _31, reg_write);
  and and_32 (and_32_out, _32, reg_write);
  Register #(.width(32)) register_29 (.D(write_data), .Q(_29O), .clk(clock), .clr(and_29_out));  // open: en
  Register #(.width(32)) register_30 (.D(write_data), .Q(_30O), .clk(clock), .clr(and_30_out));  // open: en
  Register #(.width(32)) register_31 (.D(write_data), .Q(_31O), .clk(clock), .clr(and_31_out));  // open: en
  Register #(.width(32)) register_32 (.D(write_data), .Q(_32O), .clk(clock), .clr(and_32_out));  // open: en
  Multiplexer #(.select(5), .width(32)) multiplexer_1 (
    .in0(_1O), .in1(_2O), .in2(_3O), .in3(_4O), .in4(_5O), .in5(_6O), .in6(_7O), .in7(_8O), .in8(_9O),
    .in9(_10O), .in10(_11O), .in11(_12O), .in12(_13O), .in13(_14O), .in14(_15O), .in15(_16O), .in16(_17O),
    .in17(_18O), .in18(_19O), .in19(_20O), .in20(_1O), .in21(_22O), .in22(_23O), .in23(_24O), .in24(_25O),
    .in25(_26O), .in26(_27O), .in27(_28O), .in28(_29O), .in29(_30O), .in30(_31O), .in31(_32O),
    .out(read_data_1), .sel(read_register_1));  // open: en
  Multiplexer #(.select(5), .width(32)) multiplexer_2 (
    .in0(_1O), .in1(_2O), .in2(_3O), .in3(_4O), .in4(_5O), .in5(_6O), .in6(_7O), .in7(_8O), .in8(_9O),
    .in9(_10O), .in10(_11O), .in11(_12O), .in12(_13O), .in13(_14O), .in14(_15O), .in15(_16O), .in16(_17O),
    .in17(_18O), .in18(_19O), .in19(_20O), .in20(_1O), .in21(_22O), .in22(_23O), .in23(_24O), .in24(_25O),
    .in25(_26O), .in26(_27O), .in27(_28O), .in28(_29O), .in29(_30O), .in30(_31O), .in31(_32O),
    .out(read_data_2), .sel(read_register_2));  // open: en

  // Other names for the same wires on the sheet: en = clock; in[31:0] = write_data
endmodule
